# Fritzing sketch Door Sketch (saved by Fritzing 0.9.3b)
breadboards: 1

parts:
  Grove1 = Grove OLED 128x96
  S1 = Round Pushbutton
  Part2 = Bluetooth HC-05 Macho
  J1 = Basic Servo
  kEYPAD_MATRICIAL_3 = KEYPAD 4x3
  Part6 = Arduino Nano (Rev3.0) (ICSP)
  JACK1 = 2.1mm Barrel Jack with Terminal Block

nets:
  N1: Grove1.SDA, Part6.A4
  N2: Grove1.SCL, Part6.A5
  N3: S1.leg0, Part6.D3
  N4: S1.leg1, Part6.GND
  N5: Part2.TXD, Part6.D0/RX
  N6: Part2.RXD, Part6.D1/TX
  VCC: Part2.VCC, J1.vcc, Part6.5V
  GND: Part2.GND, J1.gnd, JACK1.NEG
  N7: J1.pulse, Part6.D11/MOSI
  N8: kEYPAD_MATRICIAL_3.col1, Part6.D10
  N9: kEYPAD_MATRICIAL_3.arrow1, Part6.D9
  N10: kEYPAD_MATRICIAL_3.col2, Part6.D8
  N11: kEYPAD_MATRICIAL_3.arrow2, Part6.D7
  N12: kEYPAD_MATRICIAL_3.col3, Part6.D6
  N13: kEYPAD_MATRICIAL_3.arrow3, Part6.D5
  N14: kEYPAD_MATRICIAL_3.arrow4, Part6.D4
  N15: Part6.VIN, JACK1.POS
