# Fritzing sketch Height Sketch (saved by Fritzing 0.9.3b)

parts:
  Part1 = Arduino Nano (Rev3.0)
  HC-SR04_Sensor_1 = HC-SR04 Ultrasonic Distance Sensor
  Part2 = Bluetooth HC-05 Macho
  Grove1 = Grove OLED 128x96
  U2 = LIPO-2000mAh [package=lipo-2000]
  S10 = SPST Switch [package=r_sw_th]
  S11 = Round Pushbutton
  S12 = Round Pushbutton

nets:
  N1: Part1.D1/TX, Part2.RXD
  N2: Part1.D0/RX, Part2.TXD
  GND: Part1.GND, Grove1.GND
  N3: Part1.D2, S11.leg0
  N4: Part1.D3, S12.leg0
  N5: Part1.D10, HC-SR04_Sensor_1.TRIG
  N6: Part1.D11/MOSI, HC-SR04_Sensor_1.ECHO
  N7: Part1.VIN, S10.P
  5V: Part1.5V, Grove1.VCC
  N8: Part1.A5, Grove1.SCL
  N9: Part1.A4, Grove1.SDA
  N10: U2.+, S10.O
