# Fritzing sketch Room Sketch (saved by Fritzing 0.9.3b)
breadboards: 1

parts:
  Part2 = Arduino Due (Rev2b)
  S4 = Pushbutton [package="[THT]"]
  RHT1 = Humidity and Temperature Sensor RHT03
  Part3 = 4x Matrix LED 8x8 with MAX7219 [part_number=FC-16]
  Part4 = 4x Matrix LED 8x8 with MAX7219 [part_number=FC-16]
  YwRobot_Power_Supply1 = YwRobot Breadboard Power Supply [part_number=545043]
  Part5 = Bluetooth HC-05 Macho
  J1 = Basic Servo
  J2 = Basic Servo

nets:
  GND: Part2.GND, Part4.GND, YwRobot_Power_Supply1.GND#13, Part5.GND, J1.gnd, J2.gnd
  VCC: Part2.VIN, Part4.VCC, YwRobot_Power_Supply1.VCC#9, Part5.VCC, J2.vcc
  N1: Part2.D9_PWM, J2.pulse
  N2: Part2.D10_PWM/SS0, Part4.CS
  N3: Part2.D13_PWM, Part3.CS
  N4: Part2.D0/RX, Part5.RXD
  N5: Part2.D1/TX, Part5.TXD
  N6: Part2.D2_PWM, RHT1.GND_1
  N7: Part2.D3_PWM, S4.Pin_3, S4.Pin_4
  N8: S4.Pin_1, S4.Pin_2, RHT1.Data-signal, Part3.GND, YwRobot_Power_Supply1.GND#11
  N9: RHT1.GND_2, Part3.VCC, YwRobot_Power_Supply1.VCC#5
  N10: Part3.CLK, Part4.CLK
  N11: Part3.DIN, Part4.DIN

custom parts:
  4x Matrix LED 8x8 with MAX7219: FC-16
  YwRobot Breadboard Power Supply: The YwRobot Breadboard Power Supply (MB-V2) has two power rails; they can be 5V or 3V3. Power to the module can be provided through the female USB socket or through the A10 (female) 2.1mm power jack.
